// Logisim project parte2_cabeada.circ as structural Verilog: 3 circuits, main circuit UC_cabeada
module UC_cabeada (
  input  RESET,
  input  CLK,
  input  B,
  output SF2,
  output SF1,
  output SF0,
  output PCWrite,
  output MemRead,
  output IRWrite,
  output ALUSrcB0,
  output RegWrite,
  output ALUSrcA,
  output PCWriteCond,
  output PCSource,
  output ALUOp0,
  output ALUSrcB1,
  output ALUOp1
);

  wire and_1_out, and_2_out, D0_out, D1_out, D2_out, nB, nQ0, nQ1, nQ2;

  not not_1 (nB, B);
  and and_1 (and_1_out, ALUOp1, nQ0);
  and and_2 (and_2_out, nQ1, ALUSrcB1, nB);
  and and_3 (ALUSrcB0, nQ2, nQ1, nQ0);
  and and_4 (RegWrite, ALUOp1, ALUSrcB1);
  or or_1 (ALUSrcA, ALUOp0, ALUOp1);
  and D2 (D2_out, nQ1, ALUSrcB1, B);
  or D1 (D1_out, and_1_out, and_2_out);
  and D0 (D0_out, nQ2, nQ0);
  D_Flip_Flop F2 (.D(D2_out), .clk(CLK), .Q(ALUOp0), .Qn(nQ2), .reset(RESET));  // open: preset
  D_Flip_Flop F1 (.D(D1_out), .clk(CLK), .Q(ALUOp1), .Qn(nQ1), .reset(RESET));  // open: preset
  D_Flip_Flop F0 (.D(D0_out), .clk(CLK), .Q(ALUSrcB1), .Qn(nQ0), .reset(RESET));  // open: preset

  assign IRWrite = ALUSrcB0;
  assign MemRead = ALUSrcB0;
  assign PCSource = ALUOp0;
  assign PCWrite = ALUSrcB0;
  assign PCWriteCond = ALUOp0;
  assign SF0 = ALUSrcB1;
  assign SF1 = ALUOp1;
  assign SF2 = ALUOp0;

  // Other names for the same wires on the sheet: Q0 = ALUSrcB1; Q1 = ALUOp1; Q2 = ALUOp0

  // Notes on the sheet:
  //   BLOCO S0
  //   MAQUINA DE ESTADOS
  //   SAÍDAS
endmodule

module JunMain (
  input  RESET,
  input  B
);

  wire CLK_out;
  wire [2:0] ESTADO;

  Clock CLK (.out(CLK_out));
  Hex_Digit_Display hex_digit_display_1 (.value({1'b0, ESTADO}));  // open: dp
  UC_cabeada uc_cabeada_1 (
    .RESET(RESET), .CLK(CLK_out), .B(B), .SF2(ESTADO[2]), .SF1(ESTADO[1]), .SF0(ESTADO[0]));  // open: PCWrite, MemRead, IRWrite, ALUSrcB0, RegWrite, ALUSrcA, PCWriteCond, PCSource, ALUOp0, ALUSrcB1, ALUOp1
endmodule

module CPU (
  input  RESET,
  input  B
);

  wire ALUSrcA, CLK, IRWrite, MemRead, PCSource, PCWrite, PCWriteCond, RegWrite;
  wire [1:0] ALUOp, ALUSrcB;
  wire [2:0] ESTADO;
  wire [3:0] END_ROM;
  wire [7:0] IR, rom_1_data;
  wire [7:4] PC;

  ROM #(.addrWidth(4)) rom_1 (.addr(END_ROM), .data(rom_1_data));
  Clock u_CLK (.out(CLK));
  Register u_PC (.D(8'h4), .en(PCWrite), .clk(CLK), .Q({PC, END_ROM}), .clr(RESET));
  UC_cabeada uc_cabeada_1 (
    .RESET(RESET), .CLK(CLK), .B(B), .SF2(ESTADO[2]), .SF1(ESTADO[1]), .SF0(ESTADO[0]), .PCWrite(PCWrite),
    .MemRead(MemRead), .IRWrite(IRWrite), .ALUSrcB0(ALUSrcB[0]), .RegWrite(RegWrite), .ALUSrcA(ALUSrcA),
    .PCWriteCond(PCWriteCond), .PCSource(PCSource), .ALUOp0(ALUOp[0]), .ALUSrcB1(ALUSrcB[1]),
    .ALUOp1(ALUOp[1]));
  Register register_1 (.D(rom_1_data), .en(IRWrite), .clk(CLK), .Q(IR), .clr(RESET));
  Multiplexer #(.width(8)) multiplexer_1 ();  // open: in0, in1, out, sel

  // Other names for the same wires on the sheet: PC[3:0] = END_ROM

  // Notes on the sheet:
  //   contents of rom_1 (hex, n*v repeats v):
  //   11 0 0 0 22
endmodule
