// Logisim project parte1_cache.circ as structural Verilog: 3 circuits, main circuit main
module main (
  input  ZerarCache,
  input  Clock,
  input  [5:0] EnderecoA5_A0,
  input  Acessar,
  input  HabilitarTeste,
  output [2:0] Rotulo,
  output [1:0] Indice,
  output Deslocamento,
  output [2:0] RotuloGuardado
);

  wire and_1_out, and_2_out, and_3_out, and_4_out, and_5_out, and_6_out, and_7_out, and_8_out, and_9_out,
       and_10_out, and_11_out, detectorprimos_1_detectap, Linha0_q, Linha1_q, Linha2_q, Linha3_q,
       multiplexer_2_out, multiplexer_3_out, multiplexer_4_out, multiplexer_5_out, multiplexer_6_out,
       multiplexer_7_out, not_1_out, not_2_out, not_3_out, not_4_out, or_1_out, undriven, xor1bit_1_x,
       xor1bit_2_x, xor1bit_3_x;
  wire [2:0] Tag0_q, Tag1_q, Tag2_q, Tag3_q;
  wire [3:0] counter_1_q, counter_2_q;
  wire [5:0] detectorprimos_1_a5aa0;

  DetectorPrimos detectorprimos_1 (
    .Clear(ZerarCache), .Clk(Clock), .A5aA0(detectorprimos_1_a5aa0), .DetectaP(detectorprimos_1_detectap));
  Multiplexer #(.width(6)) multiplexer_1 (
    .in0(EnderecoA5_A0), .in1(detectorprimos_1_a5aa0), .out({Rotulo, Indice, Deslocamento}),
    .sel(HabilitarTeste));
  Multiplexer multiplexer_2 (
    .in0(Acessar), .in1(detectorprimos_1_detectap), .out(multiplexer_2_out), .sel(HabilitarTeste));
  Multiplexer multiplexer_3 (.in0(Linha0_q), .in1(1'b1), .out(multiplexer_3_out), .sel(and_5_out));
  not not_1 (not_1_out, Indice[1]);
  D_Flip_Flop Linha0 (.D(multiplexer_3_out), .clk(Clock), .Q(Linha0_q), .reset(ZerarCache));  // open: Qn, preset
  not not_2 (not_2_out, Indice[0]);
  Multiplexer multiplexer_4 (.in0(Linha1_q), .in1(1'b1), .out(multiplexer_4_out), .sel(and_6_out));
  D_Flip_Flop Linha1 (.D(multiplexer_4_out), .clk(Clock), .Q(Linha1_q), .reset(ZerarCache));  // open: Qn, preset
  and and_1 (and_1_out, not_2_out, not_1_out);
  and and_2 (and_2_out, Indice[0], not_1_out);
  and and_3 (and_3_out, not_2_out, Indice[1]);
  and and_4 (and_4_out, Indice[0], Indice[1]);
  Multiplexer multiplexer_5 (.in0(Linha2_q), .in1(1'b1), .out(multiplexer_5_out), .sel(and_7_out));
  D_Flip_Flop Linha2 (.D(multiplexer_5_out), .clk(Clock), .Q(Linha2_q), .reset(ZerarCache));  // open: Qn, preset
  Multiplexer #(.select(2)) multiplexer_6 (
    .in0(Linha0_q), .in1(Linha1_q), .in2(Linha2_q), .in3(Linha3_q), .out(multiplexer_6_out), .sel(Indice));
  and and_5 (and_5_out, and_1_out, not_3_out, multiplexer_2_out);
  and and_6 (and_6_out, and_2_out, not_3_out, multiplexer_2_out);
  and and_7 (and_7_out, and_3_out, not_3_out, multiplexer_2_out);
  and and_8 (and_8_out, and_4_out, not_3_out, multiplexer_2_out);
  Multiplexer multiplexer_7 (.in0(Linha3_q), .in1(1'b1), .out(multiplexer_7_out), .sel(and_8_out));
  Register #(.width(3)) Tag0 (.D(Rotulo), .clk(Clock), .Q(Tag0_q), .clr(ZerarCache));  // open: en
  D_Flip_Flop Linha3 (.D(multiplexer_7_out), .clk(Clock), .Q(Linha3_q), .reset(ZerarCache));  // open: Qn, preset
  Register #(.width(3)) Tag1 (.D(Rotulo), .clk(Clock), .Q(Tag1_q), .clr(ZerarCache));  // open: en
  Register #(.width(3)) Tag2 (.D(Rotulo), .clk(Clock), .Q(Tag2_q), .clr(ZerarCache));  // open: en
  Register #(.width(3)) Tag3 (.D(Rotulo), .en(undriven), .clk(Clock), .Q(Tag3_q), .clr(ZerarCache));
  Multiplexer #(.select(2), .width(3)) multiplexer_8 (
    .in0(Tag0_q), .in1(Tag1_q), .in2(Tag2_q), .in3(Tag3_q), .out(RotuloGuardado), .sel(Indice));
  Xor1Bit xor1bit_1 (.A(Rotulo[0]), .B(RotuloGuardado[0]), .X(xor1bit_1_x));
  and and_9 (and_9_out, multiplexer_6_out, not_4_out);
  Xor1Bit xor1bit_2 (.A(RotuloGuardado[2]), .B(Rotulo[2]), .X(xor1bit_2_x));
  Xor1Bit xor1bit_3 (.A(Rotulo[1]), .B(RotuloGuardado[1]), .X(xor1bit_3_x));
  not not_3 (not_3_out, and_9_out);
  or or_1 (or_1_out, xor1bit_2_x, xor1bit_3_x, xor1bit_1_x);
  not not_4 (not_4_out, or_1_out);
  and and_10 (and_10_out, and_9_out, multiplexer_2_out);
  and and_11 (and_11_out, not_3_out, multiplexer_2_out);
  Counter #(.max('hf), .width(4)) counter_1 (
    .clr(ZerarCache), .up(1'b1), .count(and_10_out), .clk(Clock), .Q(counter_1_q));  // open: load, D, carry
  Counter #(.max('hf), .width(4)) counter_2 (
    .clr(ZerarCache), .up(1'b1), .count(and_11_out), .clk(Clock), .Q(counter_2_q));  // open: load, D, carry
  Hex_Digit_Display ContAcertos (.value(counter_1_q));  // open: dp
  Hex_Digit_Display ContFaltas (.value(counter_2_q));  // open: dp

  // Notes on the sheet:
  //   Offset
  //   Decodificador
  //   Seleciona linha
  //   TAG_T2_T1_T0
  //   Atuliza0
  //   Atuliza1
  //   Atuliza2
  //   Atuliza3
  //   ZeraRegistradores
  //   Bit_de_Validade
  //   Comparador
  //   T2xorS2
  //   T1xorS1
  //   T0xorS0
  //   Acerto
  //   Falta
  //   Zera os Contadores
endmodule

module Xor1Bit (
  input  A,
  input  B,
  output X
);

  wire and_1_out, and_2_out, not_1_out, not_2_out;

  not not_1 (not_1_out, B);
  not not_2 (not_2_out, A);
  and and_1 (and_1_out, A, not_1_out);
  and and_2 (and_2_out, not_2_out, B);
  or or_1 (X, and_1_out, and_2_out);
endmodule

module DetectorPrimos (
  input  Clear,
  input  Clk,
  output [5:0] A5aA0,
  output DetectaP
);

  wire and_1_out, and_2_out, not_1_out;

  Counter #(.max('h7), .width(3)) Contador_0a7 (
    .clr(Clear), .clk(Clk), .Q(A5aA0[5:3]));  // open: load, up, count, D, carry
  not not_1 (not_1_out, A5aA0[5]);
  and and_1 (and_1_out, A5aA0[3], A5aA0[5]);
  and and_2 (and_2_out, A5aA0[4], not_1_out);
  or or_1 (DetectaP, and_1_out, and_2_out);

  assign A5aA0[2:0] = 3'b000;

  // Notes on the sheet:
  //   A0
  //   A1
  //   A2
  //   A5
  //   SaidaV0aV3
  //   A4
  //   A3
endmodule
