// Logisim project parte1_memoria.circ as structural Verilog: 3 circuits, main circuit main
module main (
  input  Escrita,
  input  Clock,
  input  [7:0] Dados,
  input  [5:0] endereco,
  output ErroDeParidade,
  output [7:0] Saida_dados,
  output out_7
);

  wire and_1_out, and_2_out, and_3_out, CS_IO_out, CS_RAM_out, CS_REG_out, DetParidade_dout, not_1_out,
       not_2_out, not_3_out, not_4_out, xor8_a_1_out_2, xor8_a_2_out_2;
  wire [7:0] IOinterface_dout, M0Rom_data, M1Ram1_dout, RegisterBank_dout;

  not not_1 (not_1_out, endereco[5]);
  not not_2 (not_2_out, endereco[4]);
  and CS_ROM (out_7, not_1_out, not_2_out);
  and CS_RAM (CS_RAM_out, not_1_out, endereco[4]);
  and CS_REG (CS_REG_out, endereco[5], not_2_out);
  and CS_IO (CS_IO_out, endereco[5], endereco[4]);
  and and_1 (and_1_out, Escrita, CS_RAM_out);
  ROM #(.addrWidth(4)) M0Rom (.addr(endereco[3:0]), .data(M0Rom_data));
  RAM #(.addrWidth(4), .clearpin("true")) M1Ram1 (
    .addr(endereco[3:0]), .we(and_1_out), .clk(Clock), .din(Dados), .dout(M1Ram1_dout));  // open: oe, clr
  and and_2 (and_2_out, Escrita, CS_REG_out);
  and and_3 (and_3_out, Escrita, CS_IO_out);
  RAM #(.addrWidth(4)) RegisterBank (
    .addr(endereco[3:0]), .we(and_2_out), .clk(Clock), .din(Dados), .dout(RegisterBank_dout));  // open: oe
  RAM #(.addrWidth(4)) IOinterface (
    .addr(endereco[3:0]), .we(and_3_out), .clk(Clock), .din(Dados), .dout(IOinterface_dout));  // open: oe
  Multiplexer #(.select(2), .width(8)) multiplexer_1 (
    .in0(M0Rom_data), .in1(M1Ram1_dout), .in2(RegisterBank_dout), .in3(IOinterface_dout), .out(Saida_dados),
    .sel(endereco[5:4]));
  RAM #(.addrWidth(4), .dataWidth(1)) DetParidade (
    .addr(endereco[3:0]), .we(and_1_out), .clk(Clock), .din(not_3_out), .dout(DetParidade_dout));  // open: oe
  Xor8_A xor8_a_1 (.in_1(Dados), .out_2(xor8_a_1_out_2));
  Xor8_A xor8_a_2 (.in_1(M1Ram1_dout), .out_2(xor8_a_2_out_2));
  not not_3 (not_3_out, xor8_a_1_out_2);
  not not_4 (not_4_out, xor8_a_2_out_2);
  xor_1bit xor_1bit_1 (.A(DetParidade_dout), .B(not_4_out), .S(ErroDeParidade));

  // Notes on the sheet:
  //   Circuito Sencíavel a  borda de Subida
  //   Decodificador2para4
  //   contents of M0Rom (hex, n*v repeats v):
  //   aa ae
  //   Paridade na Escrita
  //   Paridade na leitura
endmodule

module xor_1bit (
  input  A,
  input  B,
  output S
);

  wire and_1_out, and_2_out, not_1_out, not_2_out;

  not not_1 (not_1_out, B);
  not not_2 (not_2_out, A);
  and and_1 (and_1_out, A, not_1_out);
  and and_2 (and_2_out, not_2_out, B);
  or or_1 (S, and_1_out, and_2_out);
endmodule

module Xor8_A (
  input  [7:0] in_1,
  output out_2
);

  wire xor_1bit_1_s, xor_1bit_2_s, xor_1bit_3_s, xor_1bit_4_s, xor_1bit_5_s, xor_1bit_6_s;

  xor_1bit xor_1bit_1 (.A(in_1[0]), .B(in_1[1]), .S(xor_1bit_1_s));
  xor_1bit xor_1bit_2 (.A(xor_1bit_1_s), .B(in_1[2]), .S(xor_1bit_2_s));
  xor_1bit xor_1bit_3 (.A(xor_1bit_2_s), .B(in_1[3]), .S(xor_1bit_3_s));
  xor_1bit xor_1bit_4 (.A(xor_1bit_3_s), .B(in_1[4]), .S(xor_1bit_4_s));
  xor_1bit xor_1bit_5 (.A(xor_1bit_4_s), .B(in_1[5]), .S(xor_1bit_5_s));
  xor_1bit xor_1bit_6 (.A(xor_1bit_5_s), .B(in_1[6]), .S(xor_1bit_6_s));
  xor_1bit xor_1bit_7 (.A(xor_1bit_6_s), .B(in_1[7]), .S(out_2));
endmodule
